// Digital circuit frontpanel.dig as structural Verilog
module frontpanel (
  input  [7:0] value,
  input  [1:0] dest,
  input  [1:0] src,
  input  tworeg,
  output [31:0] R0,
  output [31:0] R1,
  output [31:0] R2,
  output [31:0] R3,
  output [31:0] L,
  output [1:0] rs,
  output [1:0] rd,
  output [31:0] R,
  output [3:0] PC,
  output [31:0] target,
  output [1:0] rd_2,
  output [1:0] rs_2,
  output [1:0] rd_3,
  output [31:0] R_2
);

  wire add, add_out, advance_out, assembler_1_p9, assembler_1_p10, decoder_1_p1, decoder_1_p2, decoder_1_p6,
       execute_1_p4, fetch_1_p8, jump, jump_out, mode_out, move, move_out, pmshim_1_p6, pmshim_1_p7,
       pmshim_1_p8;
  wire [3:0] pmshim_1_p4;
  wire [15:0] pmshim_1_p5, Program_d;

  Button u_add (.out(add_out));
  Button u_move (.out(move_out));
  Button u_jump (.out(jump_out));
  LED programming (.in(mode_out));
  DipSwitch mode (.out(mode_out));
  // assembler assembler_1: pin names not known; wires that end beside it: mode_out, value, dest, src, tworeg, add_out, move_out, jump_out, assembler_1_p9, assembler_1_p10
  // pmshim pmshim_1: pin names not known; wires that end beside it: PC, assembler_1_p9, assembler_1_p10, pmshim_1_p4, pmshim_1_p5, pmshim_1_p6, pmshim_1_p7, pmshim_1_p8
  EEPROMDualPort #(.AddrBits(4), .isProgramMemory("true"), .Bits(16)) Program (
    .A(pmshim_1_p4), .Din(pmshim_1_p5), .str(pmshim_1_p6), .C(pmshim_1_p7), .ld(pmshim_1_p8), .D(Program_d));
  Button advance (.out(advance_out));
  // fetch fetch_1: pin names not known; wires that end beside it: mode_out, assembler_1_p9, Program_d, advance_out, R, jump, PC, fetch_1_p8
  LED jump_2 (.in(jump));
  LED move_2 (.in(move));
  LED add_2 (.in(add));
  // decoder decoder_1: pin names not known; wires that end beside it: decoder_1_p1, decoder_1_p2, fetch_1_p8, rs, rd, decoder_1_p6, L, R, move, add, jump
  // execute execute_1: pin names not known; wires that end beside it: decoder_1_p6, L, R, execute_1_p4
  // regfile regfile_1: pin names not known; wires that end beside it: rs, rd, execute_1_p4, advance_out, decoder_1_p1, decoder_1_p2, R0, R1, R2, R3

  assign R_2 = R;
  assign rd_2 = rd;
  assign rd_3 = rd;
  assign rs_2 = rs;
  assign target = R;

  // Notes on the sheet:
  //   rj45 Creates
  //   Fibonacci
  //   0: R2 = R2 + 1
  //   1: R2 = R2 + R1
  //   2: R3 = R2
  //   3: R1 = R1 + R2
  //   4: R3 = R1
  //   5: jump 1
  //   contents of Program (hex, n*v repeats v):
  //   120,161,1bd,191,17d,10e
  //   PC =
  //   R
  //   =
  //   ( R
  //   )
  //   +
endmodule
